// Logisim project MpMp25.circ as structural Verilog: 3 circuits, main circuit main
module main (
);

  wire and_1_out, clock_1_out, comparator_1_eq;
  wire [1:0] counter_1_q_3;
  wire [3:0] counter_1_q, counter_1_q_2, rom_1_data;
  wire [7:0] alu_1_flag_out, rom_2_data, rom_3_data, rom_4_data;

  Clock clock_1 (.out(clock_1_out));
  Hex_Digit_Display hex_digit_display_1 (.value({2'b00, counter_1_q_3}));  // open: dp
  Hex_Digit_Display hex_digit_display_2 (.value(counter_1_q_2));  // open: dp
  and and_1 (and_1_out, clock_1_out, comparator_1_eq);
  Hex_Digit_Display hex_digit_display_3 (.value(counter_1_q));  // open: dp
  Counter #(.max('h3ff), .width(10)) counter_1 (
    .Q({counter_1_q_3, counter_1_q_2, counter_1_q}), .clk(and_1_out));  // open: load, D, count, carry, up, clr
  ROM #(.addrWidth(10), .dataWidth(4)) rom_1 (.addr({counter_1_q_3, counter_1_q_2, counter_1_q}), .data(rom_1_data));
  ROM #(.addrWidth(10)) rom_2 (.addr({counter_1_q_3, counter_1_q_2, counter_1_q}), .data(rom_2_data));
  ROM #(.addrWidth(10)) rom_3 (.addr({counter_1_q_3, counter_1_q_2, counter_1_q}), .data(rom_3_data));
  ROM #(.addrWidth(10)) rom_4 (.addr({counter_1_q_3, counter_1_q_2, counter_1_q}), .data(rom_4_data));
  ALU alu_1 (
    .CMD_15_12(rom_1_data), .Op0(rom_4_data), .Op1(rom_2_data), .Flag_Out(alu_1_flag_out),
    .Result(alu_1_flag_out));  // open: Flag_In
  Comparator comparator_1 (.a(alu_1_flag_out), .b(rom_3_data), .eq(comparator_1_eq));  // open: gt, lt
  LED led_1 (.in(comparator_1_eq));

  // Notes on the sheet:
  //   contents of rom_2 (hex, n*v repeats v):
  //   4 5 6
  //   contents of rom_3 (hex, n*v repeats v):
  //   5 7 8
  //   contents of rom_4 (hex, n*v repeats v):
  //   1 2 3
endmodule

module ALU (
  input  [7:0] Op0,
  input  [7:0] Op1,
  input  [3:0] CMD_15_12,
  input  [7:0] Flag_In,
  output [7:0] Result,
  output [7:0] Flag_Out
);

  wire adder_1_cout, multiplexer_2_out, Z_out;
  wire [7:0] adder_1_out, Flag_Select_data, subtractor_1_out;

  ROM #(.addrWidth(4)) Flag_Select (.addr(CMD_15_12), .data(Flag_Select_data));
  Adder adder_1 (.a(Op0), .b(Op1), .out(adder_1_out), .cout(adder_1_cout));  // open: cin
  Subtractor subtractor_1 (.a(Op1), .b(Op0), .out(subtractor_1_out));  // open: bin, bout
  Multiplexer #(.select(4), .width(8)) multiplexer_1 (
    .in0(adder_1_out), .in1(subtractor_1_out), .out(Result), .sel(CMD_15_12));  // open: in2, in3, in4, in5, in6, in7, in8, in9, in10, in11, in12, in13, in14, in15
  Multiplexer #(.select(4)) multiplexer_2 (
    .in0(adder_1_cout), .out(multiplexer_2_out), .sel(CMD_15_12));  // open: in1, in2, in3, in4, in5, in6, in7, in8, in9, in10, in11, in12, in13, in14, in15
  Multiplexer multiplexer_3 (.in0(Flag_In[0]), .in1(Z_out), .out(Flag_Out[0]), .sel(Flag_Select_data[0]));
  Multiplexer multiplexer_4 (.in0(Flag_In[1]), .in1(multiplexer_2_out), .out(Flag_Out[1]), .sel(Flag_Select_data[1]));
  Multiplexer multiplexer_5 (.in0(Flag_In[2]), .out(Flag_Out[2]), .sel(Flag_Select_data[2]));  // open: in1
  Multiplexer multiplexer_6 (.in0(Flag_In[3]), .out(Flag_Out[3]));  // open: in1, sel
  nor Z (Z_out, Result[0], Result[1], Result[2], Result[3], Result[4], Result[5], Result[6], Result[7]);

  assign Flag_Out[7:4] = Flag_In[7:4];

  // Notes on the sheet:
  //   contents of Flag_Select (hex, n*v repeats v):
  //   3
  //     XXX,overflow_O, carry_C, zero_Z
  //   C_Flag
  //   Z_Flag
  //   C_Flag
  //   O_Flag
endmodule

module CU (
  input  CLK,
  input  RST,
  input  [15:0] Instruction
);

  wire [1:0] Cyclecounter_q;
  wire [15:0] register_1_q;

  Register #(.width(16)) register_1 (.D(Instruction), .clk(CLK), .Q(register_1_q), .clr(RST));  // open: en
  Counter #(.max('h3), .width(2)) Cyclecounter (
    .Q(Cyclecounter_q), .clk(CLK), .clr(RST));  // open: load, D, count, carry, up
  ROM #(.addrWidth(9), .dataWidth(32)) rom_1 (.addr({register_1_q[7], register_1_q[11], register_1_q[6], register_1_q[15:12], Cyclecounter_q}));  // open: data

  // Notes on the sheet:
  //   IMOPb[7]
  //   IMOPa[11]
  //   CMD[6]
  //   CMD0[15...12]
endmodule
